# Fritzing sketch Circuit diagram (saved by Fritzing 0.9.3b)
breadboards: 1

parts:
  Part1 = Arduino Uno (Rev3)  # not connected
  Part2 = Arduino Ethernet Shield (Rev3)
  T1 = LM35 Temperature Sensor [package="TO92 [THT]"]
  LED1 = LED - 5mm [color="Red (633nm)" package="5 mm [THT]"]
  LCD1 = LCD screen  # not connected
  R1 = Photocell (LDR) [package=THT]
  LED2 = LED - 5mm [color="Red (633nm)" package="5 mm [THT]"]
  R2 = Resistor [tolerance=±5% resistance=220 package=THT]

nets:
  GND: Part2.GND, T1.GND, LED1.anode, LED2.anode, R2.Pin_1
  N1: Part2.A0, R1.pin_1, R2.Pin_0
  N2: Part2.A1, T1.Vout
  N3: Part2.PWM_D6, LED2.cathode
  N4: Part2.D7, LED1.cathode
  N5: Part2.3V3, T1.+Vs, R1.pin_0

notes:
  Arduino Uno with Ethernet Shield
