# Fritzing sketch currentBreadboardDiagram (saved by Fritzing 0.9.3b)
circuit board: 5.83065cm x 11.2504cm

parts:
  Arduino_Pro_Mini = Arduino Mini (Rev5)
  Raspberry_Pi_3 = Raspberry Pi 3 [part_number=RPI-3-V1.2]
  DS1 = DS18B20 1-Wire Temperature Sensor [part_number=DS18B20]
  R5 = Resistor [tolerance=±5% resistance=4k package="1206 [SMD]"]

nets:
  GND: Arduino_Pro_Mini.GND, Raspberry_Pi_3.GND, DS1.GND
  VCC: Arduino_Pro_Mini.VCC, Raspberry_Pi_3.5V
  5V: Arduino_Pro_Mini.5V, DS1.VDD
  N1: Arduino_Pro_Mini.A0, DS1.DQ, R5.Pin_0
  N2: Arduino_Pro_Mini.TX, Raspberry_Pi_3.GIPO15
  N3: Arduino_Pro_Mini.RX, Raspberry_Pi_3.GIPO14

notes:
  Raspberry Pi has the camera module attached and is powered by the USB port
  4k ohm resistor between data and power
  DS18B20 is waterproof and on a long wire
  Arduino and Raspberry Pi are connected via 5v dc and ground. With Rx on the Raspberry Pi connected to Tx on the Arduino and Tx on the Raspberry Pi connected to Rx on the Arduino
